// Logisim project ArquiteturaDeComputadores.circ as structural Verilog: 5 circuits, main circuit main
module main (
  input  [3:0] in_1,
  input  [3:0] in_2,
  output out_3,
  output out_4,
  output [3:0] out_5,
  output [3:0] out_6
);

  Sub4 sub4_1 (.A(in_1), .B(in_2), .OVERFLOW(out_3), .CARRY_IN(1'b0), .\SUBTRAÇÃO (out_5));
  Add4 add4_1 (.A(in_1), .B(in_2), .OVERFLOW(out_4), .CARRY_IN(1'b0), .SOMA(out_6));
endmodule

module Add1 (
  input  A,
  input  B,
  input  CARRY_IN,
  output S,
  output CARRY_OUT
);

  wire and_1_out, and_2_out, or_1_out, xor_1_out;

  xor xor_1 (xor_1_out, A, B);
  or or_1 (or_1_out, B, CARRY_IN);
  xor xor_2 (S, xor_1_out, CARRY_IN);
  and and_1 (and_1_out, B, CARRY_IN);
  and and_2 (and_2_out, or_1_out, A);
  or or_2 (CARRY_OUT, and_2_out, and_1_out);
endmodule

module Add4 (
  input  [3:0] A,
  input  [3:0] B,
  input  CARRY_IN,
  output OVERFLOW,
  output [3:0] SOMA
);

  wire add1_1_carry_out, add1_3_carry_out, add1_4_carry_out;

  Add1 add1_1 (.A(A[2]), .B(B[2]), .CARRY_IN(add1_3_carry_out), .S(SOMA[2]), .CARRY_OUT(add1_1_carry_out));
  Add1 add1_2 (.A(A[3]), .B(B[3]), .CARRY_IN(add1_1_carry_out), .S(SOMA[3]), .CARRY_OUT(OVERFLOW));
  Add1 add1_3 (.A(A[1]), .B(B[1]), .CARRY_IN(add1_4_carry_out), .S(SOMA[1]), .CARRY_OUT(add1_3_carry_out));
  Add1 add1_4 (.A(A[0]), .B(B[0]), .CARRY_IN(CARRY_IN), .S(SOMA[0]), .CARRY_OUT(add1_4_carry_out));
endmodule

module Sub1 (
  input  A,
  input  B,
  input  CARRY_IN,
  output S,
  output CARRY_OUT
);

  wire and_1_out, and_2_out, not_1_out, or_1_out, xor_1_out;

  xor xor_1 (xor_1_out, A, B);
  or or_1 (or_1_out, B, CARRY_IN);
  xor xor_2 (S, xor_1_out, CARRY_IN);
  not not_1 (not_1_out, A);
  and and_1 (and_1_out, B, CARRY_IN);
  and and_2 (and_2_out, or_1_out, not_1_out);
  or or_2 (CARRY_OUT, and_2_out, and_1_out);
endmodule

module Sub4 (
  input  [3:0] A,
  input  [3:0] B,
  input  CARRY_IN,
  output OVERFLOW,
  output [3:0] \SUBTRAÇÃO 
);

  wire sub1_2_carry_out, sub1_3_carry_out, sub1_4_carry_out;

  Sub1 sub1_1 (.A(A[3]), .B(B[3]), .CARRY_IN(sub1_2_carry_out), .S(\SUBTRAÇÃO [3]), .CARRY_OUT(OVERFLOW));
  Sub1 sub1_2 (.A(A[2]), .B(B[2]), .CARRY_IN(sub1_3_carry_out), .S(\SUBTRAÇÃO [2]), .CARRY_OUT(sub1_2_carry_out));
  Sub1 sub1_3 (.A(A[1]), .B(B[1]), .CARRY_IN(sub1_4_carry_out), .S(\SUBTRAÇÃO [1]), .CARRY_OUT(sub1_3_carry_out));
  Sub1 sub1_4 (.A(A[0]), .B(B[0]), .CARRY_IN(CARRY_IN), .S(\SUBTRAÇÃO [0]), .CARRY_OUT(sub1_4_carry_out));
endmodule
